// Logisim project cap_2_exercises.circ as structural Verilog
module _2_1_b (
  input  a,
  input  b,
  input  c,
  output y
);

  wire and_1_out, and_2_out, not_1_out, not_2_out, not_3_out;

  not not_1 (not_1_out, a);
  not not_2 (not_2_out, b);
  not not_3 (not_3_out, c);
  and and_1 (and_1_out, not_1_out, not_2_out, not_3_out);
  and and_2 (and_2_out, a, b, c);
  or or_1 (y, and_1_out, and_2_out);
endmodule

module _2_1_c (
  input  a,
  input  b,
  input  c,
  output y,
  output out_5
);

  wire and_1_out, and_2_out, and_3_out, not_1_out, not_2_out, not_3_out;

  not not_1 (not_1_out, c);
  not not_2 (not_2_out, a);
  not not_3 (not_3_out, b);
  and and_1 (and_1_out, not_2_out, not_1_out);
  and and_2 (and_2_out, not_3_out, not_1_out);
  and and_3 (and_3_out, a, c);
  Multiplexer #(.select(2), .enable("false")) multiplexer_1 (
    .in0(not_1_out), .in1(not_1_out), .in2(1'b1), .in3(c), .out(out_5), .sel({a, b}));
  or or_1 (y, and_1_out, and_2_out, and_3_out);

  // Notes on the sheet:
  //   This multiplexer imitates the circuit above.
endmodule

module _2_17_a (
  input  a,
  input  b,
  input  c,
  output y,
  output out_5,
  output out_6
);

  wire and_1_out, and_2_out, and_3_out, and_4_out, not_1_out, not_2_out, not_3_out, not_4_out, not_5_out,
       not_6_out;

  not not_1 (not_1_out, c);
  not not_2 (not_2_out, a);
  and and_1 (and_1_out, not_1_out, not_2_out);
  or or_1 (out_5, and_1_out, b);
  Multiplexer #(.select(2), .enable("false")) multiplexer_1 (
    .in0(1'b1), .in1(b), .in2(b), .in3(b), .out(out_6), .sel({a, c}));
  not not_3 (not_3_out, a);
  not not_4 (not_4_out, b);
  not not_5 (not_5_out, c);
  not not_6 (not_6_out, c);
  and and_2 (and_2_out, b, c);
  and and_3 (and_3_out, not_3_out, not_4_out, not_5_out);
  and and_4 (and_4_out, b, not_6_out);
  or or_2 (y, and_2_out, and_3_out, and_4_out);
endmodule

module _2_17_b (
  input  a,
  input  b,
  output y,
  output out_4
);

  wire and_1_out, and_2_out, nor_1_out, nor_2_out, not_1_out, not_2_out, not_3_out, not_4_out;

  not not_1 (not_1_out, a);
  not not_2 (not_2_out, a);
  not not_3 (not_3_out, b);
  and and_1 (and_1_out, not_1_out, b);
  and and_2 (and_2_out, not_2_out, not_3_out);
  not not_4 (not_4_out, b);
  and and_3 (out_4, not_1_out, b);
  nor nor_1 (nor_1_out, a, and_1_out, and_2_out);
  nor nor_2 (nor_2_out, a, not_4_out);
  or or_1 (y, nor_1_out, nor_2_out);
endmodule

module _2_26 (
  input  in_1,
  input  in_2,
  input  in_3,
  input  in_4,
  input  in_5,
  output out_6
);

  wire nand_1_out, nand_2_out, nand_3_out;

  nand nand_1 (nand_1_out, in_1, in_2);
  nand nand_2 (nand_2_out, in_3, in_4);
  nand nand_3 (nand_3_out, nand_1_out, nand_2_out);
  nand nand_4 (out_6, nand_3_out, in_5);
endmodule

module _2_28 (
  input  a,
  input  b,
  input  c,
  input  d,
  output y
);

  wire and_1_out, and_2_out, and_3_out, not_1_out;

  and and_1 (and_1_out, a, not_1_out);
  not not_1 (not_1_out, d);
  and and_2 (and_2_out, a, c);
  and and_3 (and_3_out, a, b);
  or or_1 (y, and_1_out, and_2_out, and_3_out);
endmodule

module _2_31 (
  input  a,
  input  b,
  input  c,
  input  d,
  output y
);

  wire and_1_out, and_2_out, and_3_out, and_4_out, not_1_out, not_2_out, not_3_out, not_4_out;

  not not_1 (not_1_out, a);
  not not_2 (not_2_out, b);
  not not_3 (not_3_out, c);
  not not_4 (not_4_out, d);
  and and_1 (and_1_out, not_1_out, d);
  and and_2 (and_2_out, c, d);
  and and_3 (and_3_out, b, d);
  and and_4 (and_4_out, a, not_2_out, not_3_out, not_4_out);
  or or_1 (y, and_1_out, and_2_out, and_3_out, and_4_out);
endmodule

module _2_40 (
  input  d,
  input  b,
  input  c,
  input  a,
  output out_5
);

  wire multiplexer_1_out;

  Multiplexer #(.select(2), .enable("false")) multiplexer_1 (
    .in0(1'b1), .in1(1'b0), .in2(1'b0), .in3(1'b0), .out(multiplexer_1_out), .sel({c, d}));
  Multiplexer #(.select(2), .enable("false")) multiplexer_2 (
    .in0(1'b1), .in1(multiplexer_1_out), .in2(multiplexer_1_out), .in3(1'b0), .out(out_5), .sel({a, b}));
endmodule

module _2_42 (
  input  b,
  input  a,
  input  c,
  output out_4
);

  wire nor_1_out;

  nor nor_1 (nor_1_out, a, c);
  Multiplexer #(.enable("false")) multiplexer_1 (.in0(nor_1_out), .in1(1'b1), .out(out_4), .sel(b));
endmodule
