// Logisim project cap_3_theory_exercises.circ as structural Verilog
module sr_latch (
  input  R,
  input  S,
  output Q,
  output nQ
);

  nor nor_1 (Q, R, nQ);
  nor nor_2 (nQ, Q, S);
endmodule

module d_latch (
  input  D,
  output Q,
  output nQ
);

  wire and_1_out, and_2_out, clock_1_out, not_1_out;

  Clock clock_1 (.out(clock_1_out));
  not not_1 (not_1_out, D);
  and and_1 (and_1_out, clock_1_out, not_1_out);
  and and_2 (and_2_out, clock_1_out, D);
  nor nor_1 (Q, and_1_out, nQ);
  nor nor_2 (nQ, Q, and_2_out);
endmodule

module d_flip_flop (
  input  D,
  output Q,
  output nQ,
  output nQ_2
);

  wire and_1_out, and_2_out, and_3_out, and_4_out, clock_1_out, nor_1_out, not_1_out, not_2_out, not_3_out;

  not not_1 (not_1_out, D);
  and and_1 (and_1_out, not_2_out, not_1_out);
  and and_2 (and_2_out, not_2_out, D);
  not not_2 (not_2_out, clock_1_out);
  nor nor_1 (nor_1_out, and_1_out, nQ);
  nor nor_2 (nQ, nor_1_out, and_2_out);
  Clock clock_1 (.out(clock_1_out));
  not not_3 (not_3_out, nor_1_out);
  and and_3 (and_3_out, clock_1_out, not_3_out);
  and and_4 (and_4_out, clock_1_out, nor_1_out);
  nor nor_3 (Q, and_3_out, nQ_2);
  nor nor_4 (nQ_2, Q, and_4_out);

  // Notes on the sheet:
  //   Master D latch
  //   Slave D latch
endmodule

module one_hot_encode (
  input  in_1
);

  wire clock_1_out, d_ff_1_q, d_ff_2_q, d_ff_3_q;

  Clock clock_1 (.out(clock_1_out));
  D_Flip_Flop d_ff_1 (.clk(clock_1_out), .D(d_ff_3_q), .Q(d_ff_1_q), .reset(in_1));  // open: Qn, preset, en
  D_Flip_Flop d_ff_2 (.clk(clock_1_out), .D(d_ff_1_q), .Q(d_ff_2_q), .reset(in_1));  // open: Qn, preset, en
  D_Flip_Flop d_ff_3 (.clk(clock_1_out), .D(d_ff_2_q), .Q(d_ff_3_q), .preset(in_1));  // open: Qn, en, reset
  LED led_1 (.in(d_ff_3_q));

  // Notes on the sheet:
  //   Divide by 3 counter with one-hot encodig states
endmodule

module snail_example (
  input  Input
);

  wire and_1_out, and_2_out, and_3_out, and_4_out, CLK_out, d_ff_1_q, d_ff_2_q, d_ff_3_q, d_ff_4_q, d_ff_5_q,
       not_1_out, not_2_out, not_3_out, not_4_out, or_1_out;

  not not_1 (not_1_out, Input);
  Clock CLK (.out(CLK_out));
  or or_1 (or_1_out, d_ff_4_q, d_ff_5_q);
  not not_2 (not_2_out, d_ff_4_q);
  not not_3 (not_3_out, d_ff_5_q);
  D_Flip_Flop d_ff_1 (.clk(CLK_out), .D(not_1_out), .Q(d_ff_1_q));  // open: Qn, preset, en, reset
  and and_1 (and_1_out, Input, or_1_out);
  and and_2 (and_2_out, Input, not_2_out, not_3_out);
  and and_3 (and_3_out, Input, d_ff_1_q);
  D_Flip_Flop d_ff_2 (.clk(CLK_out), .D(d_ff_3_q), .Q(d_ff_2_q));  // open: Qn, preset, en, reset
  D_Flip_Flop d_ff_3 (.clk(CLK_out), .D(Input), .Q(d_ff_3_q));  // open: Qn, preset, en, reset
  D_Flip_Flop d_ff_4 (.clk(CLK_out), .D(and_1_out), .Q(d_ff_4_q));  // open: Qn, preset, en, reset
  D_Flip_Flop d_ff_5 (.clk(CLK_out), .D(and_2_out), .Q(d_ff_5_q));  // open: Qn, preset, en, reset
  LED OUTPUT (.in(and_3_out));
  not not_4 (not_4_out, d_ff_2_q);
  LED OUTPUT_2 (.in(d_ff_5_q));
  and and_4 (and_4_out, not_4_out, d_ff_3_q);
  LED OUTPUT_3 (.in(and_4_out));

  // Notes on the sheet:
  //   Moore FSM design for snail, 4 states
  //   Moore FSM design for snail, 3 states only
  //   Mealy FSM design for snail, 2 states only
endmodule

module _3_7 (
  input  in_1,
  input  in_2,
  input  in_3,
  input  in_4,
  output out_5,
  output out_6,
  output out_7,
  output out_8
);

  wire nor_1_out, nor_2_out;

  nand nand_1 (out_5, in_1, out_6);
  nand nand_2 (out_6, out_5, in_2);
  nor nor_1 (nor_1_out, in_3, nor_2_out);
  nor nor_2 (nor_2_out, nor_1_out, in_4);
  not not_1 (out_7, nor_1_out);
  not not_2 (out_8, nor_2_out);
endmodule

module _3_9 (
);

  wire clock_1_out, d_ff_1_q, not_1_out, t_ff_1_q, t_ff_2_q, t_ff_3_q, t_ff_4_q;

  Clock clock_1 (.out(clock_1_out));
  not not_1 (not_1_out, d_ff_1_q);
  D_Flip_Flop d_ff_1 (.clk(clock_1_out), .D(not_1_out), .Q(d_ff_1_q));  // open: Qn, preset, en, reset
  T_Flip_Flop #(.trigger("falling")) t_ff_1 (.clk(clock_1_out), .T(1'b1), .Q(t_ff_1_q));  // open: Qn, preset, reset, en
  T_Flip_Flop #(.trigger("falling")) t_ff_2 (.clk(t_ff_1_q), .T(1'b1), .Q(t_ff_2_q));  // open: Qn, preset, reset, en
  T_Flip_Flop #(.trigger("falling")) t_ff_3 (.clk(t_ff_2_q), .T(1'b1), .Q(t_ff_3_q));  // open: Qn, preset, reset, en
  T_Flip_Flop #(.trigger("falling")) t_ff_4 (.clk(t_ff_3_q), .T(1'b1), .Q(t_ff_4_q));  // open: Qn, preset, reset, en
  LED led_1 (.in(d_ff_1_q));
  LED led_2 (.in(t_ff_1_q));
  LED led_3 (.in(t_ff_2_q));
  LED led_4 (.in(t_ff_3_q));
  LED led_5 (.in(t_ff_4_q));

  // Notes on the sheet:
  //   T flip flop with a D flip flop and an inverter
  //   4 bits counter with 4 cascade T flip flop falling edge
endmodule

module _3_13_15 (
  input  in_1,
  input  D,
  input  D_2,
  input  in_4,
  output Q,
  output nQ,
  output nQ_2,
  output Q_2,
  output nQ_3,
  output nQ_4
);

  wire and_1_out, and_2_out, and_3_out, and_4_out, and_5_out, and_6_out, and_7_out, and_8_out, and_9_out,
       and_10_out, clock_1_out, clock_2_out, nor_1_out, nor_3_out, not_1_out, not_2_out, not_3_out,
       not_4_out, not_5_out, not_6_out, not_7_out, or_1_out, or_2_out, or_3_out, or_4_out, or_5_out, or_6_out;

  not not_1 (not_1_out, D);
  not not_2 (not_2_out, D_2);
  and and_1 (and_1_out, not_3_out, not_1_out);
  and and_2 (and_2_out, not_3_out, D);
  and and_3 (and_3_out, not_4_out, not_2_out);
  and and_4 (and_4_out, not_4_out, D_2);
  or or_1 (or_1_out, in_1, and_1_out);
  or or_2 (or_2_out, and_2_out, in_4);
  and and_5 (and_5_out, not_7_out, and_3_out);
  or or_3 (or_3_out, and_4_out, in_4);
  not not_3 (not_3_out, clock_1_out);
  nor nor_1 (nor_1_out, or_1_out, nQ);
  nor nor_2 (nQ, nor_1_out, or_2_out);
  not not_4 (not_4_out, clock_2_out);
  nor nor_3 (nor_3_out, and_5_out, nQ_3);
  nor nor_4 (nQ_3, nor_3_out, or_3_out);
  Clock clock_1 (.out(clock_1_out));
  Clock clock_2 (.out(clock_2_out));
  not not_5 (not_5_out, nor_1_out);
  not not_6 (not_6_out, nor_3_out);
  not not_7 (not_7_out, in_4);
  and and_6 (and_6_out, clock_1_out, not_5_out);
  and and_7 (and_7_out, clock_1_out, nor_1_out);
  and and_8 (and_8_out, clock_2_out, not_6_out);
  and and_9 (and_9_out, clock_2_out, nor_3_out);
  or or_4 (or_4_out, in_1, and_6_out);
  or or_5 (or_5_out, and_7_out, in_4);
  and and_10 (and_10_out, not_7_out, and_8_out);
  or or_6 (or_6_out, and_9_out, in_4);
  nor nor_5 (Q, or_4_out, nQ_2);
  nor nor_6 (nQ_2, Q, or_5_out);
  nor nor_7 (Q_2, and_10_out, nQ_4);
  nor nor_8 (nQ_4, Q_2, or_6_out);
endmodule

module _3_25 (
  input  Input,
  input  Reset,
  output out_3
);

  wire and_1_out, and_2_out, and_3_out, and_4_out, and_5_out, and_6_out, clock_1_out, d_ff_1_q, d_ff_2_q,
       d_ff_3_q, not_1_out, not_2_out, or_1_out, or_2_out;

  not not_1 (not_1_out, Input);
  not not_2 (not_2_out, d_ff_3_q);
  and and_1 (and_1_out, Input, d_ff_3_q);
  and and_2 (and_2_out, Input, d_ff_2_q);
  and and_3 (and_3_out, Input, not_2_out);
  Clock clock_1 (.out(clock_1_out));
  and and_4 (and_4_out, not_1_out, d_ff_2_q);
  or or_1 (or_1_out, and_1_out, and_2_out);
  or or_2 (or_2_out, and_2_out, and_3_out);
  D_Flip_Flop d_ff_1 (.clk(clock_1_out), .D(and_4_out), .Q(d_ff_1_q), .reset(Reset));  // open: Qn, preset, en
  D_Flip_Flop d_ff_2 (.clk(clock_1_out), .D(or_1_out), .Q(d_ff_2_q), .reset(Reset));  // open: Qn, preset, en
  D_Flip_Flop d_ff_3 (.clk(clock_1_out), .D(or_2_out), .Q(d_ff_3_q), .reset(Reset));  // open: Qn, preset, en
  and and_5 (and_5_out, Input, d_ff_1_q);
  and and_6 (and_6_out, not_1_out, d_ff_2_q, d_ff_3_q);
  or or_3 (out_3, and_5_out, and_6_out);

  // Notes on the sheet:
  //   Mealy FSM (Snail daughter)
endmodule

module _3_27 (
  input  Reset,
  output out_2,
  output out_3,
  output out_4
);

  wire clock_1_out, d_ff_1_q, d_ff_2_q, d_ff_3_q, d_ff_4_q, d_ff_5_q, d_ff_6_q, d_ff_7_q, d_ff_8_q;

  Clock clock_1 (.out(clock_1_out));
  D_Flip_Flop d_ff_1 (.clk(clock_1_out), .D(d_ff_8_q), .Q(d_ff_1_q), .preset(Reset));  // open: Qn, en, reset
  D_Flip_Flop d_ff_2 (.clk(clock_1_out), .D(d_ff_1_q), .Q(d_ff_2_q), .reset(Reset));  // open: Qn, preset, en
  or or_1 (out_4, d_ff_2_q, d_ff_3_q, d_ff_6_q, d_ff_7_q);
  D_Flip_Flop d_ff_3 (.clk(clock_1_out), .D(d_ff_2_q), .Q(d_ff_3_q), .reset(Reset));  // open: Qn, preset, en
  or or_2 (out_3, d_ff_3_q, d_ff_4_q, d_ff_5_q, d_ff_6_q);
  D_Flip_Flop d_ff_4 (.clk(clock_1_out), .D(d_ff_3_q), .Q(d_ff_4_q), .reset(Reset));  // open: Qn, preset, en
  D_Flip_Flop d_ff_5 (.clk(clock_1_out), .D(d_ff_4_q), .Q(d_ff_5_q), .reset(Reset));  // open: Qn, preset, en
  or or_3 (out_2, d_ff_5_q, d_ff_6_q, d_ff_7_q, d_ff_8_q);
  D_Flip_Flop d_ff_6 (.clk(clock_1_out), .D(d_ff_5_q), .Q(d_ff_6_q), .reset(Reset));  // open: Qn, preset, en
  D_Flip_Flop d_ff_7 (.clk(clock_1_out), .D(d_ff_6_q), .Q(d_ff_7_q), .reset(Reset));  // open: Qn, preset, en
  D_Flip_Flop d_ff_8 (.clk(clock_1_out), .D(d_ff_7_q), .Q(d_ff_8_q), .reset(Reset));  // open: Qn, preset, en

  // Notes on the sheet:
  //   3 bit modulo 8 Gray counter
endmodule

module _3_29 (
  input  A,
  input  B,
  output out_3
);

  wire and_1_out, and_2_out, and_3_out, clock_1_out, d_ff_1_q;

  Clock clock_1 (.out(clock_1_out));
  D_Flip_Flop d_ff_1 (.clk(clock_1_out), .D(A), .Q(d_ff_1_q));  // open: Qn, preset, en, reset
  and and_1 (and_1_out, d_ff_1_q, A);
  and and_2 (and_2_out, d_ff_1_q, B);
  and and_3 (and_3_out, A, B);
  or or_1 (out_3, and_1_out, and_2_out, and_3_out);
endmodule

module _3_31 (
  input  in_1,
  output out_2
);

  wire and_1_out, clock_1_out, d_ff_1_q, d_ff_2_q, not_1_out, not_2_out, or_1_out;

  Clock clock_1 (.out(clock_1_out));
  or or_1 (or_1_out, d_ff_2_q, not_1_out);
  not not_1 (not_1_out, d_ff_1_q);
  D_Flip_Flop d_ff_1 (.clk(clock_1_out), .D(or_1_out), .Q(d_ff_1_q));  // open: Qn, preset, en, reset
  not not_2 (not_2_out, d_ff_2_q);
  and and_1 (and_1_out, in_1, not_2_out);
  D_Flip_Flop d_ff_2 (.clk(clock_1_out), .D(and_1_out), .Q(d_ff_2_q));  // open: Qn, preset, en, reset
  or or_2 (out_2, d_ff_2_q, d_ff_1_q);
endmodule
