// Logisim project d_latch_flip_flop.circ as structural Verilog: 1 circuit, main circuit main
module main (
  input  R,
  input  in_2,
  input  D,
  input  CLK,
  input  EN,
  input  S,
  input  in_7,
  input  CLK_2,
  input  D_2,
  output Q,
  output out_11,
  output nQ,
  output Q_2,
  output nQ_2
);

  wire and_1_out, and_2_out, not_1_out;

  // D_Flip_Flop F1: pin names not known; wires that end beside it: D, CLK, EN, in_2, in_7, out_11
  not not_1 (not_1_out, D_2);
  and and_1 (and_1_out, CLK_2, not_1_out);
  and and_2 (and_2_out, CLK_2, D_2);
  nor nor_1 (Q, R, nQ);
  nor nor_2 (nQ, Q, S);
  nor nor_3 (Q_2, and_1_out, nQ_2);
  nor nor_4 (nQ_2, Q_2, and_2_out);

  // Notes on the sheet:
  //   D latch
  //   SR latch
endmodule
