// Logisim project fsm_traffic_lights.circ as structural Verilog: 1 circuit, main circuit main
module main (
  input  Puch_Button_A,
  input  Puch_Button_B,
  output out_3,
  output out_4
);

  wire and_1_out, and_2_out, and_3_out, and_4_out, and_5_out, clock_1_out, nor_1_out, not_1_out, not_2_out,
       not_3_out, not_4_out, not_5_out, not_6_out, not_7_out, or_1_out, or_2_out, or_3_out, xor_1_out;

  not not_1 (not_1_out, out_3);
  not not_2 (not_2_out, out_4);
  not not_3 (not_3_out, Puch_Button_A);
  not not_4 (not_4_out, out_4);
  not not_5 (not_5_out, Puch_Button_B);
  not not_6 (not_6_out, out_3);
  not not_7 (not_7_out, out_4);
  and and_1 (and_1_out, not_1_out, not_2_out, not_3_out);
  and and_2 (and_2_out, out_3, not_4_out, not_5_out);
  xor xor_1 (xor_1_out, out_3, out_4);
  or or_1 (or_1_out, and_1_out, and_2_out);
  and and_3 (and_3_out, out_3, not_7_out);
  LED led_1 (.in(or_2_out));
  and and_4 (and_4_out, out_4, not_6_out);
  LED led_2 (.in(and_4_out));
  LED led_3 (.in(nor_1_out));
  nor nor_1 (nor_1_out, out_4, out_3);
  and and_5 (and_5_out, out_4, out_3);
  Clock clock_1 (.out(clock_1_out));
  or or_2 (or_2_out, and_3_out, and_5_out);
  D_Flip_Flop d_ff_1 (.clk(clock_1_out), .D(xor_1_out), .Q(out_3));  // open: Qn, preset, en, reset
  D_Flip_Flop d_ff_2 (.clk(clock_1_out), .D(or_1_out), .Q(out_4));  // open: Qn, preset, en, reset
  LED led_4 (.in(or_3_out));
  LED led_5 (.in(and_5_out));
  LED led_6 (.in(and_3_out));
  or or_3 (or_3_out, nor_1_out, and_4_out);

  // Notes on the sheet:
  //   Finite State Machine example: Traffic lights on intersection 
  //   Traffic light 1
  //   Traffic light 2
endmodule
