// Logisim project seven_segment_disp.circ as structural Verilog: 1 circuit, main circuit seven-segment
module seven_segment (
  output a,
  output b,
  output c,
  output d,
  output e,
  output f,
  output g
);

  wire and_1_out, and_2_out, and_3_out, and_4_out, and_5_out, and_6_out, and_7_out, and_8_out, and_9_out,
       and_10_out, and_11_out, and_12_out, and_13_out, and_14_out, and_15_out, and_16_out, and_17_out,
       clock_1_out, not_1_out, not_2_out, not_3_out, not_4_out, not_5_out, not_6_out, not_7_out, not_8_out,
       not_9_out, not_10_out, not_11_out, not_12_out, not_13_out, not_14_out, not_15_out, not_16_out,
       not_17_out, not_18_out, not_19_out, not_20_out, not_21_out, not_22_out, not_23_out;
  wire [3:0] counter_1_q;

  Clock clock_1 (.out(clock_1_out));
  Counter #(.width(4), .max('hf)) counter_1 (
    .Q(counter_1_q), .clk(clock_1_out), .clr(and_1_out));  // open: load, D, count, carry
  not not_1 (not_1_out, counter_1_q[2]);
  not not_2 (not_2_out, counter_1_q[0]);
  and and_1 (and_1_out, counter_1_q[1], counter_1_q[3], not_2_out, not_1_out);
  not not_3 (not_3_out, counter_1_q[2]);
  not not_4 (not_4_out, counter_1_q[0]);
  not not_5 (not_5_out, counter_1_q[1]);
  not not_6 (not_6_out, counter_1_q[0]);
  not not_7 (not_7_out, counter_1_q[1]);
  not not_8 (not_8_out, counter_1_q[2]);
  not not_9 (not_9_out, counter_1_q[0]);
  not not_10 (not_10_out, counter_1_q[2]);
  not not_11 (not_11_out, counter_1_q[0]);
  not not_12 (not_12_out, counter_1_q[1]);
  not not_13 (not_13_out, counter_1_q[2]);
  not not_14 (not_14_out, counter_1_q[0]);
  not not_15 (not_15_out, counter_1_q[0]);
  not not_16 (not_16_out, counter_1_q[1]);
  not not_17 (not_17_out, counter_1_q[0]);
  not not_18 (not_18_out, counter_1_q[1]);
  not not_19 (not_19_out, counter_1_q[0]);
  not not_20 (not_20_out, counter_1_q[2]);
  not not_21 (not_21_out, counter_1_q[1]);
  not not_22 (not_22_out, counter_1_q[0]);
  and and_2 (and_2_out, not_3_out, not_4_out);
  and and_3 (and_3_out, counter_1_q[2], counter_1_q[0]);
  not not_23 (not_23_out, counter_1_q[2]);
  and and_4 (and_4_out, not_5_out, not_6_out);
  and and_5 (and_5_out, counter_1_q[1], counter_1_q[0]);
  or or_1 (c, not_7_out, counter_1_q[0], counter_1_q[2]);
  and and_6 (and_6_out, not_8_out, not_9_out);
  and and_7 (and_7_out, not_10_out, counter_1_q[1]);
  and and_8 (and_8_out, counter_1_q[1], not_11_out);
  and and_9 (and_9_out, counter_1_q[2], not_12_out, counter_1_q[0]);
  and and_10 (and_10_out, not_13_out, not_14_out);
  and and_11 (and_11_out, counter_1_q[1], not_15_out);
  and and_12 (and_12_out, not_16_out, not_17_out);
  and and_13 (and_13_out, counter_1_q[2], not_18_out);
  and and_14 (and_14_out, counter_1_q[2], not_19_out);
  and and_15 (and_15_out, not_20_out, counter_1_q[1]);
  and and_16 (and_16_out, counter_1_q[2], not_21_out);
  and and_17 (and_17_out, counter_1_q[2], not_22_out);
  or or_2 (a, and_2_out, counter_1_q[1], and_3_out, counter_1_q[3]);
  or or_3 (b, not_23_out, and_4_out, and_5_out);
  or or_4 (d, and_6_out, and_7_out, and_8_out, and_9_out, counter_1_q[3]);
  or or_5 (e, and_10_out, and_11_out);
  or or_6 (f, and_12_out, and_13_out, and_14_out, counter_1_q[3]);
  or or_7 (g, and_15_out, and_16_out, and_17_out, counter_1_q[3]);
  _7_Segment_Display u_7_segment_display_1 (.g(g), .f(f), .a(a), .b(b), .e(e), .d(d), .c(c));  // open: dp

  // Notes on the sheet:
  //   Resets when count = 0b1010
endmodule
